// Digital circuit Lab02.dig as structural Verilog
module Lab02 (
  input  A,
  input  B,
  input  C,
  input  D,
  output Fa,
  output Fb,
  output Fc,
  output Fd,
  output Fe,
  output Ff,
  output Fg
);

  wire A_n, and_1_out, and_2_out, and_3_out, and_4_out, and_5_out, and_6_out, and_7_out, and_8_out,
       and_9_out, and_10_out, and_11_out, and_12_out, and_13_out, and_14_out, and_15_out, and_16_out,
       and_17_out, and_18_out, and_19_out, and_20_out, and_21_out, and_22_out, and_23_out, and_24_out,
       and_25_out, and_26_out, and_27_out, and_28_out, and_29_out, and_30_out, and_31_out, and_32_out, B_n,
       C_n, D_n;

  not not_1 (A_n, A);
  not not_2 (B_n, B);
  not not_3 (C_n, C);
  not not_4 (D_n, D);
  and and_1 (and_1_out, A_n, B, D);
  and and_2 (and_2_out, A_n, C);
  and and_3 (and_3_out, A, B_n, C_n);
  and and_4 (and_4_out, B_n, D_n);
  and and_5 (and_5_out, B, C);
  and and_6 (and_6_out, A_n, B_n);
  and and_7 (and_7_out, A_n, C_n, D_n);
  and and_8 (and_8_out, A_n, C, D);
  and and_9 (and_9_out, A, C_n, D);
  and and_10 (and_10_out, B_n, D_n);
  and and_11 (and_11_out, A_n, B);
  and and_12 (and_12_out, A_n, C_n);
  and and_13 (and_13_out, A_n, D);
  and and_14 (and_14_out, A, B_n);
  and and_15 (and_15_out, C_n, D);
  and and_16 (and_16_out, A_n, B_n, D_n);
  and and_17 (and_17_out, A, C_n);
  and and_18 (and_18_out, B_n, C, D);
  and and_19 (and_19_out, B, C_n, D);
  and and_20 (and_20_out, B, C, D_n);
  and and_21 (and_21_out, A, B);
  and and_22 (and_22_out, A, C);
  and and_23 (and_23_out, B_n, D_n);
  and and_24 (and_24_out, C, D_n);
  and and_25 (and_25_out, A_n, B, C_n);
  and and_26 (and_26_out, A_n, B, D_n);
  and and_27 (and_27_out, A_n, C_n, D_n);
  and and_28 (and_28_out, A, B_n);
  and and_29 (and_29_out, A, C);
  and and_30 (and_30_out, B_n, C);
  and and_31 (and_31_out, B, C_n);
  and and_32 (and_32_out, B, D_n);
  or or_1 (Fa, and_1_out, and_2_out, and_3_out, and_4_out, and_5_out);
  or or_2 (Fb, and_6_out, and_7_out, and_8_out, and_9_out, and_10_out);
  or or_3 (Fc, and_11_out, and_12_out, and_13_out, and_14_out, and_15_out);
  or or_4 (Fd, and_16_out, and_17_out, and_18_out, and_19_out, and_20_out);
  or or_5 (Fe, and_21_out, and_22_out, and_23_out, and_24_out);
  or or_6 (Ff, and_25_out, and_26_out, and_27_out, and_28_out, and_29_out);
  or or_7 (Fg, A, and_30_out, and_31_out, and_32_out);
  Seven_Seg seven_seg_1 (.a(Fa), .b(Fb), .c(Fc), .d(Fd), .e(Fe), .f(Ff), .g(Fg), .dp(1'b0));
endmodule
